# Fritzing sketch Szkic_artuditu (saved by Fritzing 0.9.3b)
breadboards: 1

parts:
  M1 = Stepper Motor - Bipolar
  Part1 = Arduino Nano (Rev3.0)
  Pololu_A1 = Pololu A4988 [package=SO16]
  U1 = VCNL4000 [package=vcnl4000]
  Part2 = BME280 Breakout
  Part3 = Bluetooth HC-05 Macho
  VCC1 = 4 x AAA Battery Mount
  C1 = Electrolytic Capacitor [capacitance=100µF package="200 mil [THT, electrolytic]"]
  Power_plug1 = Power plug
  S1 = Pushbutton [package="[THT]"]
  S2 = Pushbutton [package="[THT]"]
  U2 = HALL-EFFECT [package=sc70]
  S3 = Pushbutton [package="[THT]"]
  Q1 = LTR-301 [package=ltr-301]

nets:
  N1: M1.A, Pololu_A1.2B
  N2: M1.C, Pololu_A1.2A
  N3: M1.B, Pololu_A1.1A
  N4: M1.D, Pololu_A1.1B
  N5: Part1.D1/TX, Part3.RXD
  N6: Part1.D0/RX, Part3.TXD
  GND: Part1.GND, Pololu_A1.GND#8, U1.GND, Part2.GND, Part3.GND, VCC1.-, S1.Pin_1, S1.Pin_2, S2.Pin_1, S2.Pin_2, U2.GND, S3.Pin_1, S3.Pin_2
  N7: Part1.D3, Pololu_A1.DIR
  N8: Part1.D4, Pololu_A1.STEP
  N9: Part1.D5, Pololu_A1.MS3
  N10: Part1.D6, Pololu_A1.MS2
  N11: Part1.D7, Pololu_A1.MS1
  N12: Part1.D8, S1.Pin_3, S1.Pin_4
  N13: Part1.D9, S2.Pin_3, S2.Pin_4
  N14: Part1.D10, S3.Pin_3, S3.Pin_4
  N15: Part1.D11/MOSI, U2.OUT
  N16: Part1.D12/MISO, Q1.E
  VIN: Part1.VIN, VCC1.+, U2.VCC
  5V: Part1.5V, Pololu_A1.VDD
  N17: Part1.A5, U1.SCL, Part2.SCK/SCL
  N18: Part1.A4, U1.SDA, Part2.SDI/SDA
  3V3: Part1.3V3, U1.VDD, Part2.3.3V, Part3.VCC, Q1.C
  N19: Pololu_A1.RESET, Pololu_A1.SLEEP
  N20: Pololu_A1.GND#14, C1.-, Power_plug1.GND
  N21: Pololu_A1.VMOT, C1.+, Power_plug1.VCC
